# Fritzing sketch arduino-eurorack-diy-homogate-circuit-schematics (saved by Fritzing 0.9.9b)
breadboards: 1

parts:
  LED2 = smd LED [color="Blue (470nm)" package="0603 [SMD]"]
  Q5 = NPN-Transistor [package="SOT-23 [SMD]"]
  R15 = Resistor [tolerance=±5% resistance=10k package="2512 [SMD]"]
  TRS5 = Audio Jack (TRS) 3.5mm [package="4Ucon 08780 [THT]"]
  R16 = Resistor [tolerance=±5% resistance=1k package="2512 [SMD]"]
  R17 = Resistor [tolerance=±5% resistance=10k package="2512 [SMD]"]
  R18 = Resistor [tolerance=±5% resistance=10k package="2512 [SMD]"]
  R19 = Resistor [tolerance=±5% resistance=4.7k package="2512 [SMD]"]
  Bauteil2 = Arduino Nano (Rev3.0)
  TRS6 = Audio Jack (TRS) 3.5mm [package="4Ucon 08780 [THT]"]
  LED3 = smd LED [color="Blue (470nm)" package="0603 [SMD]"]
  Q6 = NPN-Transistor [package="SOT-23 [SMD]"]
  R21 = Resistor [tolerance=±5% resistance=4.7k package="2512 [SMD]"]
  R22 = Resistor [tolerance=±5% resistance=10k package="2512 [SMD]"]
  R24 = Resistor [tolerance=±5% resistance=10k package="2512 [SMD]"]
  D3 = Rectifier Diode [part_number=1N4001 package="300 mil [THT]"]
  R25 = Resistor [tolerance=±5% resistance=10k package="2512 [SMD]"]
  S1 = Pushbutton [package="[THT]"]
  S2 = Pushbutton [package="[THT]"]
  J3 = shrouded pin header, 16 pins [form="♂ (shrouded male)"]
  R5 = Rotary Potentiometer (Small) [maximum_resistance=100kΩ package=THT]
  R26 = Rotary Potentiometer (Small) [maximum_resistance=100kΩ package=THT]

nets:
  N1: LED2.cathode, Q5.2, R15.Pin_0, TRS5.Sleeve, Bauteil2.GND, TRS6.Sleeve, LED3.cathode, Q6.2, R22.Pin_0, D3.anode, S1.Pin_1, S1.Pin_2, S2.Pin_1, S2.Pin_2, J3.pin3, J3.pin14, R5.leg2, R26.leg2
  N2: LED2.anode, R19.Pin_1
  N3: Q5.0, R15.Pin_1, R18.Pin_1
  N4: Q5.1, R16.Pin_1, R17.Pin_0
  N5: TRS5.Tip, R16.Pin_0
  N6: R17.Pin_1, Bauteil2.5V, R24.Pin_1, R5.leg1, R26.leg1
  N7: R18.Pin_0, Bauteil2.D3
  N8: R19.Pin_0, Bauteil2.D9
  N9: Bauteil2.D2, Q6.1, R24.Pin_0
  N10: Bauteil2.D4, S2.Pin_3, S2.Pin_4
  N11: Bauteil2.D7, S1.Pin_3, S1.Pin_4
  N12: Bauteil2.D8, R21.Pin_0
  N13: Bauteil2.VIN, J3.pin6, J3.pin11
  N14: Bauteil2.A3, R26.wiper
  N15: Bauteil2.A2, R5.wiper
  N16: TRS6.Tip, R25.Pin_0
  N17: LED3.anode, R21.Pin_1
  N18: Q6.0, R22.Pin_1, D3.cathode, R25.Pin_1
  N19: J3.pin1, J3.pin16
  N20: J3.pin2, J3.pin15
  N21: J3.pin4, J3.pin13
  N22: J3.pin5, J3.pin12
  N23: J3.pin7, J3.pin10
  N24: J3.pin8, J3.pin9

notes:
  Opto-isolator Circuit
  Fairchild 6n137 fast opto-coupler, 10Mbits/s rated
  Reverse protection diode is shottky with 30V or higher rating (1N5818 is 30V peak, 1A part)
  Input capacitor C1 should be 30V rated or higher
  Input LED forward voltage ~1.4V typ at 10mA forward current
  1MHz noise cutoff using input RC Low Pass filter, with 0.4us rise time
  Input current limit resistor is two 0.25W 3.3k resistors in parallel
  1.65k delivers
  ~9mA from 15V,
  ~15mA max at rated input voltage
  ~3.7mA at low input of 7V
  max power 300mW in input resistors at max voltage
  Larger input resistor can be used at expense of raising low end input voltage limit for reliable operation
  High level output current max 20uA results in 20mV offset
  Input threshold approx 2.5mA with 1k load resistor
  Designed for inputs of between 7V and 24V, 12-15V nominal
  Ve is for strobing the output and can be left NC if not used as has internal pullup
  Output resistor allows for full output low voltage at >5mA output current
  0.1uF Vcc decoupling required close to Vcc and GND pins
  For connection to Raspberry Pi use a level converter to convert from 5V logic to 3.3V.
  Input 7V to 24V, 15V nominal, 500kHz
  Note that grounds are not joined between source and circuit.
  Example use:
  DCC decoder front end isolator feeding Arduino
  This work by hobbyistdave is licensed under a Creative Commons Attribution-ShareAlike 4.0 International License
  No warranty either express or implied is given.
  This schematic was created with Fritzing.
  Inspired by Geoff Bunza at
  http://model-railroad-hobbyist.com/node/19446
  CV GATE
  OUT
  CV GATE
  IN
  GATE LENGTH
  + OFFSET POT
  NUDGE
  < >
  POWER
  BUS
  EURORACK HOMOGATE
  https://github.com/othmar52/eurorack-homogate
